# Fritzing sketch simon-says_sketch (saved by Fritzing 0.9.3b)
breadboards: 1

parts:
  Arduino_Uno = Arduino Uno (Rev3)
  Red_Button = Pushbutton [package="[THT]"]
  R1 = Resistor [tolerance=±5% resistance=10k package=THT]
  Green_Button = Pushbutton [package="[THT]"]
  R3 = Resistor [tolerance=±5% resistance=10k package=THT]
  Yellow_Button = Pushbutton [package="[THT]"]
  R4 = Resistor [tolerance=±5% resistance=10k package=THT]
  Red_LED = LED - 5mm [color="Red (633nm)" package="5 mm [THT]"]
  R5 = Resistor [tolerance=±5% resistance=260 package=THT]
  Green_LED = LED - 5mm [color="Green (570nm)" package="5 mm [THT]"]
  R6 = Resistor [tolerance=±5% resistance=260 package=THT]
  Yellow_LED = LED - 5mm [color="Yellow (595nm)" package="5 mm [THT]"]
  R7 = Resistor [tolerance=±5% resistance=260 package=THT]
  Piezo_Speaker = Piezo Speaker
  R8 = Resistor [tolerance=±5% resistance=260 package=THT]

nets:
  N1: Arduino_Uno.A0, Red_Button.Pin_1, Red_Button.Pin_2, R1.Pin_0
  N2: Arduino_Uno.A1, Green_Button.Pin_1, Green_Button.Pin_2, R3.Pin_0
  N3: Arduino_Uno.A2, Yellow_Button.Pin_1, Yellow_Button.Pin_2, R4.Pin_0
  N4: Arduino_Uno.D12/MISO, Piezo_Speaker.pin2
  N5: Arduino_Uno.GND, R1.Pin_1, R3.Pin_1, R4.Pin_1, Red_LED.cathode, Green_LED.cathode, Yellow_LED.cathode, R8.Pin_1
  N6: Arduino_Uno.D2, R5.Pin_1
  N7: Arduino_Uno.D3_PWM, R6.Pin_1
  N8: Arduino_Uno.D4, R7.Pin_1
  N9: Arduino_Uno.5V, Red_Button.Pin_3, Red_Button.Pin_4, Green_Button.Pin_3, Green_Button.Pin_4, Yellow_Button.Pin_3, Yellow_Button.Pin_4
  N10: Red_LED.anode, R5.Pin_0
  N11: Green_LED.anode, R6.Pin_0
  N12: Yellow_LED.anode, R7.Pin_0
  N13: Piezo_Speaker.pin1, R8.Pin_0

// code stored in the sketch: sketch.ino
#define NOTE_C5  523
#define NOTE_E5  659
#define NOTE_G5  784

// Set to true if you want debug mode
const bool DEBUG_MODE = true;



// ================
//       PINS
// ================

// Buttons pins
const int RED_BUTTON = 0;
const int GREEN_BUTTON = 1;
const int YELLOW_BUTTON = 2;
// LEDs pins
const int RED_LED = 2;
const int GREEN_LED = 3;
const int YELLOW_LED = 4;
// Global button delay
const int BUTTON_DELAY = 50;
// Buzzer pin
const int BUZZER = 11;



// ================
//   GAME CONTROL
// ================

int playerNotes[100];
int aiNotes[100];

bool buzzed = false;
bool playerTurn = false;
int currentLevel = 0;
int currentNote = 0;
int difficulty = 1000;



void setup() {
  // Are we in debug mode?
  if (DEBUG_MODE) {
    Serial.begin(9600);
    Serial.println("SIMON SAYS v0.1");
    Serial.println("Reticulating splines...");
    Serial.println();
  }
  // Set pin modes
  pinMode(RED_LED, OUTPUT);
  pinMode(GREEN_LED, OUTPUT);
  pinMode(YELLOW_LED, OUTPUT);
  pinMode(BUZZER, OUTPUT);
  digitalWrite(RED_LED, LOW);
  digitalWrite(GREEN_LED, LOW);
  digitalWrite(YELLOW_LED, LOW);
}



void loop() {

  bool buttonDown = false;

  // If game has just started
  if (currentLevel == 0) {
    startNewGame();
  }

  // Check whose turn it is
  if (playerTurn) {

    // Check for Red
    if (((analogRead(RED_BUTTON) / 10) >= 10) && !buttonDown) {
      buttonDown = true;
      digitalWrite(RED_LED, HIGH);
      if (!buzzed) {
        buzz(NOTE_C5, 100);
        buzzed = true;
      }
      delay(BUTTON_DELAY);
      if ((analogRead(RED_BUTTON) / 100) <= 0) {
        digitalWrite(RED_LED, LOW);
        buttonDown = false;
        buzzed = false;
        playerNotes[currentNote] = 0;
        currentNote++;
        Serial.println("Recorded a red.");
      } else {
        Serial.println("Holding red...");
      }
    }

    // Check for Green
    if (((analogRead(GREEN_BUTTON) / 10) >= 10) && !buttonDown) {
      buttonDown = true;
      digitalWrite(GREEN_LED, HIGH);
      if (!buzzed) {
        buzz(NOTE_E5, 100);
        buzzed = true;
      }
      delay(BUTTON_DELAY);
      if ((analogRead(GREEN_BUTTON) / 100) <= 0) {
        digitalWrite(GREEN_LED, LOW);
        buttonDown = false;
        buzzed = false;
        playerNotes[currentNote] = 1;
        currentNote++;
        Serial.println("Recorded a green.");
      } else {
        Serial.println("Holding green...");
      }
    }

    // Check for Yellow
    if (((analogRead(YELLOW_BUTTON) / 10) >= 10) && !buttonDown) {
      buttonDown = true;
      digitalWrite(YELLOW_LED, HIGH);
      if (!buzzed) {
        buzz(NOTE_G5, 100);
        buzzed = true;
      }
      delay(BUTTON_DELAY);
      if ((analogRead(YELLOW_BUTTON) / 100) <= 0) {
        digitalWrite(YELLOW_LED, LOW);
        buttonDown = false;
        buzzed = false;
        playerNotes[currentNote] = 2;
        currentNote++;
        Serial.println("Recorded a yellow.");
      } else {
        Serial.println("Holding yellow...");
      }
    }

    if (currentNote == currentLevel) {
      checkSequence();
    }

  } else {
    // Simon says...
    Serial.println("Simon says...");
    for (int i = 0; i < currentLevel; i++) {
      playLight(aiNotes[i]);
      delay(difficulty);
    }
    playerTurn = true;
  }

}



void startNewGame() {

  Serial.println("Starting a new game...");
  Serial.println();

  randomSeed(millis());

  for (int i = 0; i < 100; i++) {
    aiNotes[i] = random(0, 3);
  }

  digitalWrite(RED_LED, HIGH);
  digitalWrite(GREEN_LED, HIGH);
  digitalWrite(YELLOW_LED, HIGH);

  for (int i = 0; i <= 3; i++) {
    buzz(NOTE_C5, 100);
    buzz(NOTE_E5, 100);
    buzz(NOTE_G5, 100);
  }

  digitalWrite(RED_LED, LOW);
  digitalWrite(GREEN_LED, LOW);
  digitalWrite(YELLOW_LED, LOW);

  delay(2000);

  currentLevel = 1;
  currentNote = 0;
  difficulty = 1000;
  playerTurn = false;

}



void checkSequence() {
  bool sequenceIsCorrect = true;
  Serial.println();
  Serial.println("Checking answers...");
  for (int i = 0; i < currentLevel; i++) {
    if (playerNotes[i] != aiNotes[i]) {
      sequenceIsCorrect = false;
    }
  }
  if (sequenceIsCorrect) {
    Serial.println();
    Serial.println("Answers are correct!");
    currentLevel++;
    currentNote = 0;
    playerTurn = false;
    difficulty -= 50;
    delay(1000);
  } else {
    gameOver();
  };
}



void gameOver() {
  Serial.println();
  Serial.println("Wront sequence! Game over!!");
  Serial.println();
  startNewGame();
}



void playLight(int item) {
  switch (item) {
    case 0:
      digitalWrite(RED_LED, HIGH);
      buzz(NOTE_C5, 100);
      delay(BUTTON_DELAY);
      Serial.println("Red!");
      digitalWrite(RED_LED, LOW);
      break;
    case 1:
      digitalWrite(GREEN_LED, HIGH);
      buzz(NOTE_E5, 100);
      delay(BUTTON_DELAY);
      Serial.println("Green!");
      digitalWrite(GREEN_LED, LOW);
      break;
    case 2:
      digitalWrite(YELLOW_LED, HIGH);
      buzz(NOTE_G5, 100);
      delay(BUTTON_DELAY);
      Serial.println("Yellow!");
      digitalWrite(YELLOW_LED, LOW);
      break;
  }
}



void buzz(long frequency, long length) {
  // This is from https://www.princetronics.com/supermariothemesong/
  long delayValue = 1000000 / frequency / 2;
  long numCycles = frequency * length / 1000;
  for (long i = 0; i < numCycles; i++) {
    digitalWrite(BUZZER, HIGH);
    delayMicroseconds(delayValue);
    digitalWrite(BUZZER, LOW);
    delayMicroseconds(delayValue);
  }
}
